// Digital circuit New_Address_Decode.dig as structural Verilog
module New_Address_Decode (
  input  A0,
  input  A1,
  input  A2,
  input  A3,
  input  A4,
  input  A5,
  input  A6,
  input  A7,
  input  A8,
  input  A9,
  input  A10,
  input  A11,
  input  A12,
  input  R_nW,
  input  AS,
  output RAM_2_nCE,
  output nQ4,
  output nQ5,
  output nQ6,
  output nQ7,
  output ROM_nCE,
  output RTC_nCS,
  output RAM_1_nCS,
  output nQ0,
  output _02_03_nCS,
  output nQ2,
  output _06_07_nCS,
  output nQ4_2,
  output _0A_0B_nCS,
  output _0C_0D_nCS,
  output _0E_0F_nCS
);

  wire and_1_out, and_3_out, and_4_out, and_5_out, and_6_out, and_7_out, MX1_pin12, MX1_pin13, MX1_pin15,
       MX2_pin7, MX2_pin9, MX2_pin10, MX2_pin11, MX2_pin12, MX2_pin13, MX2_pin14, MX2_pin15, nor_1_out,
       nor_2_out, not_1_out, xor_1_out;

  nor nor_1 (nor_1_out, A4, A5);
  nor nor_2 (nor_2_out, A6, A7);
  _74138 MX1 (
    .pin1(A11), .pin2(A12), .pin3(1'b0), .pin4(1'b0), .pin5(1'b0), .pin6(AS), .pin7(nQ7), .pin8(1'b0),
    .pin9(nQ6), .pin10(nQ5), .pin11(nQ4), .pin12(MX1_pin12), .pin13(MX1_pin13), .pin14(RAM_2_nCE),
    .pin15(MX1_pin15), .pin16(1'b1));
  and and_1 (and_1_out, nor_1_out, nor_2_out);
  _74138 MX2 (
    .pin1(A8), .pin2(A9), .pin3(A10), .pin4(MX1_pin15), .pin5(MX1_pin15), .pin6(AS), .pin7(MX2_pin7),
    .pin8(1'b0), .pin9(MX2_pin9), .pin10(MX2_pin10), .pin11(MX2_pin11), .pin12(MX2_pin12), .pin13(MX2_pin13),
    .pin14(MX2_pin14), .pin15(MX2_pin15), .pin16(1'b1));
  and and_2 (ROM_nCE, MX1_pin13, MX1_pin12);
  _74138 _74138_1 (
    .pin1(A1), .pin2(A2), .pin3(A3), .pin4(MX2_pin15), .pin5(MX2_pin15), .pin6(AS), .pin7(_0E_0F_nCS),
    .pin8(1'b0), .pin9(_0C_0D_nCS), .pin10(_0A_0B_nCS), .pin11(nQ4_2), .pin12(_06_07_nCS), .pin13(nQ2),
    .pin14(_02_03_nCS), .pin15(nQ0), .pin16(1'b1));
  and and_3 (and_3_out, MX2_pin13, MX2_pin12);
  and and_4 (and_4_out, MX2_pin11, MX2_pin10);
  and and_5 (and_5_out, MX2_pin9, MX2_pin7);
  and and_6 (and_6_out, and_3_out, and_4_out);
  not not_1 (not_1_out, MX2_pin14);
  and and_7 (and_7_out, and_6_out, and_5_out);
  nand nand_1 (RTC_nCS, and_1_out, not_1_out);
  xor xor_1 (xor_1_out, RTC_nCS, not_1_out);
  and and_8 (RAM_1_nCS, xor_1_out, and_7_out);

  // Notes on the sheet:
  //   R_nW: Read High, Write Low
  //   AS: Address Select
  //   RAM_2_nCE: RAM 2 ~CE
  //   nQ4: Unused
  //   nQ5: Unused
  //   nQ6: Unused
  //   nQ7: Unused
  //   nQ0: Unused
  //   nQ2: Unused
  //   nQ4_2: Unused
endmodule
